// Logisim project Circuito 3.circ as structural Verilog: 2 circuits, main circuit Exe-1
module Exe_1 (
  input  A,
  input  B,
  input  C,
  output S
);

  wire and_1_out, or_1_out, xor_1_out;

  xor xor_1 (xor_1_out, A, B);
  or or_1 (or_1_out, xor_1_out, ~B);  // OR_Gate
  and and_1 (and_1_out, ~A, or_1_out);  // AND_Gate
  or or_2 (S, and_1_out, ~C);  // OR_Gate
endmodule

module main (
  input  in_1,
  input  in_2,
  input  in_3,
  output out_4
);

  Exe_1 exe_1_1 (.A(in_1), .B(in_2), .C(in_3), .S(out_4));
endmodule
