// Logisim project Circuito 4.circ as structural Verilog: 4 circuits, main circuit main
module main (
  input  A,
  input  B,
  input  C,
  output S1,
  output S2
);

  MACRO macro_1 (.A(A), .B(B), .C(C), .S1(S1), .S2(S2));
endmodule

module MACRO (
  input  A,
  input  B,
  input  C,
  output S1,
  output S2
);

  wire and_1_out, and_2_out, and_3_out, and_4_out, and_5_out, and_6_out, and_7_out;

  and and_1 (and_1_out, ~A, B, ~C);  // AND_Gate
  and and_2 (and_2_out, A, ~B, ~C);  // AND_Gate
  and and_3 (and_3_out, A, ~B, C);  // AND_Gate
  and and_4 (and_4_out, A, B, C);
  and and_5 (and_5_out, ~A, ~B, ~C);  // AND_Gate
  and and_6 (and_6_out, ~A, B, C);  // AND_Gate
  and and_7 (and_7_out, A, B, ~C);  // AND_Gate
  or or_1 (S1, and_1_out, and_2_out, and_3_out, and_4_out);
  or or_2 (S2, and_4_out, and_2_out, and_5_out, and_6_out, and_7_out);
endmodule

module SOMADOR (
  input  in_1,
  input  in_2,
  input  in_3,
  output out_4,
  output out_5
);

  MACRO_SOMADOR macro_somador_1 (.S(out_4), .VAI_1(out_5), .A(in_1), .B(in_2), .C(in_3));
endmodule

module MACRO_SOMADOR (
  input  A,
  input  B,
  input  C,
  output S,
  output VAI_1
);

  wire and_1_out, and_2_out, and_3_out, and_4_out, and_5_out, and_6_out, and_7_out;

  and and_1 (and_1_out, ~A, ~B, C);  // AND_Gate
  and and_2 (and_2_out, ~A, B, ~C);  // AND_Gate
  and and_3 (and_3_out, A, ~B, ~C);  // AND_Gate
  and and_4 (and_4_out, A, B, C);
  and and_5 (and_5_out, ~A, B, C);  // AND_Gate
  and and_6 (and_6_out, A, ~B, C);  // AND_Gate
  and and_7 (and_7_out, A, B, ~C);  // AND_Gate
  or or_1 (S, and_1_out, and_2_out, and_3_out, and_4_out);
  or or_2 (VAI_1, and_4_out, and_5_out, and_6_out, and_7_out);
endmodule
