// Logisim project Circuito 5.circ as structural Verilog: 2 circuits, main circuit main
module main (
  input  [2:0] in_1,
  output out_2,
  output out_3,
  output out_4,
  output out_5,
  output out_6,
  output out_7,
  output out_8,
  output out_9
);

  MACRO macro_1 (
    .S0(out_2), .S1(out_3), .S2(out_4), .S3(out_5), .S4(out_6), .S5(out_7), .S6(out_8), .S7(out_9),
    .in_1(in_1));
endmodule

module MACRO (
  input  [2:0] in_1,
  output S0,
  output S1,
  output S2,
  output S3,
  output S4,
  output S5,
  output S6,
  output S7
);

  and and_1 (S0, ~in_1[2], ~in_1[1], ~in_1[0]);  // AND_Gate
  and and_2 (S1, ~in_1[2], ~in_1[1], in_1[0]);  // AND_Gate
  and and_3 (S2, ~in_1[2], in_1[1], ~in_1[0]);  // AND_Gate
  and and_4 (S3, ~in_1[2], in_1[1], in_1[0]);  // AND_Gate
  and and_5 (S4, in_1[2], ~in_1[1], ~in_1[0]);  // AND_Gate
  and and_6 (S5, in_1[2], ~in_1[1], in_1[0]);  // AND_Gate
  and and_7 (S6, in_1[2], in_1[1], ~in_1[0]);  // AND_Gate
  and and_8 (S7, in_1[2], in_1[1], in_1[0]);
endmodule
