// Logisim project Circuito 6.circ as structural Verilog: 1 circuit, main circuit main
module main (
  input  A,
  input  B,
  input  C,
  input  D,
  output A_2,
  output B_2,
  output C_2,
  output D_2,
  output E,
  output F,
  output G
);

  wire and_1_out, and_2_out, and_3_out, and_4_out, nand_1_out, nand_2_out, nand_3_out, nand_4_out,
       nand_6_out, nand_7_out, nand_8_out, nand_9_out, nand_10_out, nand_11_out, nand_12_out, nand_13_out,
       nand_14_out, nand_15_out;

  and and_1 (and_1_out, ~A, ~B, ~C, ~D);  // AND_Gate
  and and_2 (and_2_out, ~A, ~B, C, ~D);  // AND_Gate
  and and_3 (and_3_out, ~A, B, C, ~D);  // AND_Gate
  and and_4 (and_4_out, A, ~B, ~C, ~D);  // AND_Gate
  nand nand_1 (nand_1_out, ~A, ~B, ~C, D);  // NAND_Gate
  nand nand_2 (nand_2_out, ~A, B, ~C, ~D);  // NAND_Gate
  nand nand_3 (nand_3_out, ~A, B, ~C, D);  // NAND_Gate
  nand nand_4 (nand_4_out, ~A, B, C, ~D);  // NAND_Gate
  nand nand_5 (C_2, ~A, ~B, C, ~D);  // NAND_Gate
  nand nand_6 (nand_6_out, ~A, ~B, ~C, D);  // NAND_Gate
  nand nand_7 (nand_7_out, ~A, B, ~C, ~D);  // NAND_Gate
  nand nand_8 (nand_8_out, ~A, B, C, D);  // NAND_Gate
  nand nand_9 (nand_9_out, ~A, ~B, ~C, D);  // NAND_Gate
  nand nand_10 (nand_10_out, ~A, ~B, C, ~D);  // NAND_Gate
  nand nand_11 (nand_11_out, ~A, ~B, C, D);  // NAND_Gate
  nand nand_12 (nand_12_out, ~A, B, C, D);  // NAND_Gate
  nand nand_13 (nand_13_out, ~A, ~B, ~C, ~D);  // NAND_Gate
  nand nand_14 (nand_14_out, ~A, ~B, ~C, D);  // NAND_Gate
  nand nand_15 (nand_15_out, ~A, B, C, D);  // NAND_Gate
  or or_1 (A_2, nand_1_out, nand_2_out);
  or or_2 (B_2, nand_3_out, nand_4_out);
  or or_3 (D_2, nand_6_out, nand_7_out, nand_8_out);
  or or_4 (F, nand_9_out, nand_10_out, nand_11_out, nand_12_out);
  or or_5 (G, nand_13_out, nand_14_out, nand_15_out);
  or or_6 (E, and_1_out, and_2_out, and_3_out, and_4_out);
endmodule
