// Logisim project Circuito Relógio.circ as structural Verilog: 1 circuit, main circuit main
module main (
  input  [3:0] in_1,
  input  [3:0] in_2,
  input  [3:0] in_3,
  input  [3:0] in_4,
  input  [3:0] in_5,
  input  [3:0] in_6,
  input  Load
);

  wire and_1_out, and_2_out, and_3_out, and_4_out, and_5_out, and_6_out, and_7_out, and_8_out, and_9_out,
       clock_1_out, not_1_out, not_2_out, not_3_out, not_4_out, not_5_out, not_6_out, or_1_out, or_2_out,
       or_3_out, or_4_out, or_5_out, or_6_out;
  wire [3:0] counter_1_q, counter_2_q, counter_3_q, counter_4_q, counter_5_q, counter_6_q;

  not not_1 (not_1_out, Load);
  or or_1 (or_1_out, and_7_out, and_4_out);
  Counter #(.width(4), .max('hf)) counter_1 (
    .load(Load), .D(in_1), .count(not_1_out), .Q(counter_1_q), .clk(or_1_out), .clr(and_3_out));  // open: carry
  and and_1 (and_1_out, ~counter_1_q[3], ~counter_1_q[2], counter_1_q[1], ~counter_1_q[0]);  // AND_Gate
  Hex_Digit_Display hex_digit_display_1 (.value(counter_1_q));  // open: dp
  Hex_Digit_Display hex_digit_display_2 (.value(counter_2_q));  // open: dp
  Counter #(.width(4), .max('hf)) counter_2 (
    .load(Load), .D(in_2), .count(not_2_out), .Q(counter_2_q), .clk(or_2_out), .clr(or_4_out));  // open: carry
  not not_2 (not_2_out, Load);
  or or_2 (or_2_out, and_7_out, and_5_out);
  and and_2 (and_2_out, ~counter_2_q[3], counter_2_q[2], ~counter_2_q[1], ~counter_2_q[0]);  // AND_Gate
  and and_3 (and_3_out, and_1_out, and_2_out);
  and and_4 (and_4_out, counter_2_q[3], ~counter_2_q[2], counter_2_q[1], ~counter_2_q[0]);  // AND_Gate
  not not_3 (not_3_out, Load);
  or or_3 (or_3_out, and_7_out, and_6_out);
  or or_4 (or_4_out, and_4_out, and_3_out);
  Counter #(.width(4), .max('hf)) counter_3 (
    .load(Load), .D(in_3), .count(not_3_out), .Q(counter_3_q), .clk(or_3_out), .clr(and_5_out));  // open: carry
  and and_5 (and_5_out, ~counter_3_q[3], counter_3_q[2], counter_3_q[1], ~counter_3_q[0]);  // AND_Gate
  Hex_Digit_Display hex_digit_display_3 (.value(counter_3_q));  // open: dp
  Hex_Digit_Display hex_digit_display_4 (.value(counter_4_q));  // open: dp
  not not_4 (not_4_out, Load);
  or or_5 (or_5_out, and_7_out, and_8_out);
  Counter #(.width(4), .max('hf)) counter_4 (
    .load(Load), .D(in_4), .count(not_4_out), .Q(counter_4_q), .clk(or_5_out), .clr(and_6_out));  // open: carry
  and and_6 (and_6_out, counter_4_q[3], ~counter_4_q[2], counter_4_q[1], ~counter_4_q[0]);  // AND_Gate
  not not_5 (not_5_out, Load);
  Counter #(.width(4), .max('hf)) counter_5 (
    .load(Load), .D(in_5), .count(not_5_out), .Q(counter_5_q), .clk(or_6_out), .clr(and_8_out));  // open: carry
  or or_6 (or_6_out, and_7_out, and_9_out);
  and and_7 (and_7_out, Load, clock_1_out);
  and and_8 (and_8_out, ~counter_5_q[3], counter_5_q[2], counter_5_q[1], ~counter_5_q[0]);  // AND_Gate
  Hex_Digit_Display hex_digit_display_5 (.value(counter_5_q));  // open: dp
  Hex_Digit_Display hex_digit_display_6 (.value(counter_6_q));  // open: dp
  Counter #(.width(4), .max('hf)) counter_6 (
    .load(Load), .D(in_6), .count(not_6_out), .Q(counter_6_q), .clk(clock_1_out), .clr(and_9_out));  // open: carry
  not not_6 (not_6_out, Load);
  and and_9 (and_9_out, counter_6_q[3], ~counter_6_q[2], counter_6_q[1], ~counter_6_q[0]);  // AND_Gate
  Clock clock_1 (.out(clock_1_out));
endmodule
