// Logisim project Circuito2.circ as structural Verilog
module main (
  input  in_1,
  input  in_2,
  input  in_3,
  output out_4,
  output out_5
);

  ADD_1 add_1_1 (.A(in_1), .B(in_2), .S(out_5), .C(in_3), .Vai1(out_4));
endmodule

module ADD_1 (
  input  A,
  input  B,
  input  C,
  output S,
  output Vai1
);

  wire and_1_out, and_2_out, or_1_out, xor_1_out;

  xor xor_1 (xor_1_out, A, B);
  or or_1 (or_1_out, B, C);
  and and_1 (and_1_out, B, C);
  xor xor_2 (S, xor_1_out, C);
  and and_2 (and_2_out, or_1_out, A);
  or or_2 (Vai1, and_2_out, and_1_out);
endmodule

module SOMADOR_4_BITS (
  input  [3:0] A,
  input  [3:0] A_2,
  input  in_3,
  output Overflow,
  output [3:0] out_5
);

  wire add_1_2_vai1, add_1_3_vai1, add_1_4_vai1;

  // Probe on A_2
  ADD_1 add_1_1 (.A(A[3]), .B(A_2[3]), .S(out_5[3]), .C(add_1_2_vai1), .Vai1(Overflow));
  ADD_1 add_1_2 (.A(A[2]), .B(A_2[2]), .S(out_5[2]), .C(add_1_3_vai1), .Vai1(add_1_2_vai1));
  ADD_1 add_1_3 (.A(A[1]), .B(A_2[1]), .S(out_5[1]), .C(add_1_4_vai1), .Vai1(add_1_3_vai1));
  // Probe on out_5
  ADD_1 add_1_4 (.A(A[0]), .B(A_2[0]), .S(out_5[0]), .C(in_3), .Vai1(add_1_4_vai1));
  // Probe on A
endmodule
