// Logisim project Contador Assíncrono DOWN.circ as structural Verilog: 1 circuit, main circuit main
module main (
  output out_1,
  output out_2,
  output out_3,
  output out_4
);

  wire CLOCK_out;

  Clock CLOCK (.out(CLOCK_out));
  // Probe on {out_1, out_2, out_3, out_4}
  J_K_Flip_Flop j_k_ff_1 (.J(1'b1), .clk(CLOCK_out), .K(1'b1), .Q(out_4));  // open: Qn, preset, en, reset
  J_K_Flip_Flop j_k_ff_2 (.J(1'b1), .clk(out_4), .K(1'b1), .Q(out_3));  // open: Qn, preset, en, reset
  J_K_Flip_Flop j_k_ff_3 (.J(1'b1), .clk(out_3), .K(1'b1), .Q(out_2));  // open: Qn, preset, en, reset
  J_K_Flip_Flop j_k_ff_4 (.J(1'b1), .clk(out_2), .K(1'b1), .Q(out_1));  // open: Qn, preset, en, reset

  // Notes on the sheet:
  //   CONTADOR ASSÍNCRONO DOWN
endmodule
